# Fritzing sketch chuyen_dong (saved by Fritzing 0.9.3b)

parts:
  HC-SR501 = HC-SR501 Body Sensor Module
  Part2 = IoT WiFi Uno

nets:
  VCC: HC-SR501.VCC, Part2.5V
  N1: HC-SR501.OUT, Part2.GPIO2, Part2.RST
  GND: HC-SR501.GND, Part2.GND

custom parts:
  HC-SR501 Body Sensor Module: Pyroelectric Infrared PIR Motion Sensor Detector Module
  IoT WiFi Uno: ESP8266 WiFi Uno board
