# Fritzing sketch exam2 (saved by Fritzing 0.9.3b)
breadboards: 1

parts:
  Part2 = IoT WiFi Uno
  LED1 = LEDs [package=led10mm]
  DHT2 = DHT11 Humitidy and Temperature Sensor (3 pins)

nets:
  N1: Part2.GPIO12, LED1.C
  N2: Part2.5V, DHT2.DATA
  N3: Part2.GND#62, LED1.A
  N4: Part2.GND#63, DHT2.GND
  N5: Part2.GPIO04, DHT2.VDD

custom parts:
  IoT WiFi Uno: ESP8266 WiFi Uno board
  DHT11 Humitidy and Temperature Sensor (3 pins): DHT11 Humidity and Temperature Sensor (3 pins) from the design created by John De Cristofaro for Adafruit Industries.
